// Logisim project mips_cpu_g1.circ as structural Verilog
module main (
);

  IFetch ifetch_1 ();  // open: PCnext, CLK, Reset, PCplus4, instruction
endmodule

module RF (
  input  RegWrite,
  input  [4:0] WriteReg,
  input  [31:0] WriteData,
  input  CLK,
  input  Reset,
  input  [1:0] ReadReg2,
  input  [4:0] ReadReg1,
  output [31:0] ReadData1,
  output [31:0] ReadData2
);

  wire [6:0] decoder_1_out1;
  wire [7:0] decoder_1_out8, decoder_1_out16, decoder_1_out24;
  wire [31:0] ReadR0, ReadR1, ReadR2, ReadR3, ReadR4, ReadR5, ReadR6, ReadR7, ReadR8, ReadR9, ReadR10,
       ReadR11, ReadR12, ReadR13, ReadR14, ReadR15, ReadR16, ReadR17, ReadR18, ReadR19, ReadR20, ReadR21,
       ReadR22, ReadR23, ReadR24, ReadR25, ReadR26, ReadR27, ReadR28, ReadR29, ReadR30, ReadR31;

  Decoder #(.select(5)) decoder_1 (
    .out1(decoder_1_out1[0]), .out2(decoder_1_out1[1]), .out3(decoder_1_out1[2]), .out4(decoder_1_out1[3]),
    .out5(decoder_1_out1[4]), .out6(decoder_1_out1[5]), .out7(decoder_1_out1[6]), .out8(decoder_1_out8[0]),
    .out9(decoder_1_out8[1]), .out10(decoder_1_out8[2]), .out11(decoder_1_out8[3]),
    .out12(decoder_1_out8[4]), .out13(decoder_1_out8[5]), .out14(decoder_1_out8[6]),
    .out15(decoder_1_out8[7]), .out16(decoder_1_out16[0]), .out17(decoder_1_out16[1]),
    .out18(decoder_1_out16[2]), .out19(decoder_1_out16[3]), .out20(decoder_1_out16[4]),
    .out21(decoder_1_out16[5]), .out22(decoder_1_out16[6]), .out23(decoder_1_out16[7]),
    .out24(decoder_1_out24[0]), .out25(decoder_1_out24[1]), .out26(decoder_1_out24[2]),
    .out27(decoder_1_out24[3]), .out28(decoder_1_out24[4]), .out29(decoder_1_out24[5]),
    .out30(decoder_1_out24[6]), .out31(decoder_1_out24[7]), .sel(WriteReg), .en(RegWrite));  // open: out0
  Register #(.width(32)) R0 (.D(WriteData), .en(1'b0), .clk(CLK), .Q(ReadR0), .clr(Reset));
  Register #(.width(32)) R1 (.D(WriteData), .en(decoder_1_out1[0]), .clk(CLK), .Q(ReadR1), .clr(Reset));
  Register #(.width(32)) R2 (.D(WriteData), .en(decoder_1_out1[1]), .clk(CLK), .Q(ReadR2), .clr(Reset));
  Register #(.width(32)) R3 (.D(WriteData), .en(decoder_1_out1[2]), .clk(CLK), .Q(ReadR3), .clr(Reset));
  Register #(.width(32)) R4 (.D(WriteData), .en(decoder_1_out1[3]), .clk(CLK), .Q(ReadR4), .clr(Reset));
  Register #(.width(32)) R5 (.D(WriteData), .en(decoder_1_out1[4]), .clk(CLK), .Q(ReadR5), .clr(Reset));
  Register #(.width(32)) R6 (.D(WriteData), .en(decoder_1_out1[5]), .clk(CLK), .Q(ReadR6), .clr(Reset));
  Register #(.width(32)) R7 (.D(WriteData), .en(decoder_1_out1[6]), .clk(CLK), .Q(ReadR7), .clr(Reset));
  Multiplexer #(.select(5), .width(32)) multiplexer_1 (
    .in0(ReadR0), .in1(ReadR1), .in2(ReadR2), .in3(ReadR3), .in4(ReadR4), .in5(ReadR5), .in6(ReadR6),
    .in7(ReadR7), .out(ReadData1), .sel(ReadReg1));  // open: in8, in9, in10, in11, in12, in13, in14, in15, in16, in17, in18, in19, in20, in21, in22, in23, in24, in25, in26, in27, in28, in29, in30, in31
  Register #(.width(32)) R8 (.D(WriteData), .en(decoder_1_out8[0]), .clk(CLK), .Q(ReadR8), .clr(Reset));
  Register #(.width(32)) R9 (.D(WriteData), .en(decoder_1_out8[1]), .clk(CLK), .Q(ReadR9), .clr(Reset));
  Register #(.width(32)) R10 (.D(WriteData), .en(decoder_1_out8[2]), .clk(CLK), .Q(ReadR10), .clr(Reset));
  Register #(.width(32)) R11 (.D(WriteData), .en(decoder_1_out8[3]), .clk(CLK), .Q(ReadR11), .clr(Reset));
  Register #(.width(32)) R12 (.D(WriteData), .en(decoder_1_out8[4]), .clk(CLK), .Q(ReadR12), .clr(Reset));
  Register #(.width(32)) R13 (.D(WriteData), .en(decoder_1_out8[5]), .clk(CLK), .Q(ReadR13), .clr(Reset));
  Register #(.width(32)) R14 (.D(WriteData), .en(decoder_1_out8[6]), .clk(CLK), .Q(ReadR14), .clr(Reset));
  Register #(.width(32)) R15 (.D(WriteData), .en(decoder_1_out8[7]), .clk(CLK), .Q(ReadR15), .clr(Reset));
  Register #(.width(32)) R16 (.D(WriteData), .en(decoder_1_out16[0]), .clk(CLK), .Q(ReadR16), .clr(Reset));
  Register #(.width(32)) R17 (.D(WriteData), .en(decoder_1_out16[1]), .clk(CLK), .Q(ReadR17), .clr(Reset));
  Register #(.width(32)) R18 (.D(WriteData), .en(decoder_1_out16[2]), .clk(CLK), .Q(ReadR18), .clr(Reset));
  Register #(.width(32)) R19 (.D(WriteData), .en(decoder_1_out16[3]), .clk(CLK), .Q(ReadR19), .clr(Reset));
  Register #(.width(32)) R20 (.D(WriteData), .en(decoder_1_out16[4]), .clk(CLK), .Q(ReadR20), .clr(Reset));
  Register #(.width(32)) R21 (.D(WriteData), .en(decoder_1_out16[5]), .clk(CLK), .Q(ReadR21), .clr(Reset));
  Register #(.width(32)) R22 (.D(WriteData), .en(decoder_1_out16[6]), .clk(CLK), .Q(ReadR22), .clr(Reset));
  Register #(.width(32)) R23 (.D(WriteData), .en(decoder_1_out16[7]), .clk(CLK), .Q(ReadR23), .clr(Reset));
  Register #(.width(32)) R24 (.D(WriteData), .en(decoder_1_out24[0]), .clk(CLK), .Q(ReadR24), .clr(Reset));
  Register #(.width(32)) R25 (.D(WriteData), .en(decoder_1_out24[1]), .clk(CLK), .Q(ReadR25), .clr(Reset));
  Register #(.width(32)) R26 (.D(WriteData), .en(decoder_1_out24[2]), .clk(CLK), .Q(ReadR26), .clr(Reset));
  Register #(.width(32)) R27 (.D(WriteData), .en(decoder_1_out24[3]), .clk(CLK), .Q(ReadR27), .clr(Reset));
  Register #(.width(32)) R28 (.D(WriteData), .en(decoder_1_out24[4]), .clk(CLK), .Q(ReadR28), .clr(Reset));
  Register #(.width(32)) R29 (.D(WriteData), .en(decoder_1_out24[5]), .clk(CLK), .Q(ReadR29), .clr(Reset));
  Register #(.width(32)) R30 (.D(WriteData), .en(decoder_1_out24[6]), .clk(CLK), .Q(ReadR30), .clr(Reset));
  Register #(.width(32)) R31 (.D(WriteData), .en(decoder_1_out24[7]), .clk(CLK), .Q(ReadR31), .clr(Reset));
endmodule

module IFetch (
  input  [31:0] PCnext,
  input  CLK,
  input  Reset,
  output [31:0] PCplus4,
  output [31:0] instruction
);

  wire [31:0] PCreg_q;

  Register #(.width(32)) PCreg (.D(PCnext), .clk(CLK), .Q(PCreg_q), .clr(Reset));  // open: en
  // Probe on PCreg_q
  Adder #(.width(32)) adder_1 (.a(PCreg_q), .b(32'h4), .out(PCplus4));  // open: cin, cout
  // Probe on PCreg_q[25:2]
  ROM #(.addrWidth(24), .dataWidth(32)) rom_1 (.addr(PCreg_q[25:2]), .data(instruction));

  // Notes on the sheet:
  //   contents of rom_1 (hex, n*v repeats v):
  //   12 24 23 7ae
endmodule

module IBreakdown (
  input  [31:0] Instruction,
  output [5:0] Op,
  output [4:0] rs,
  output [4:0] rt,
  output [4:0] rd,
  output [5:0] shamp,
  output [5:0] funct,
  output [15:0] fmm,
  output [25:0] address
);


  assign Op = Instruction[31:26];
endmodule
